# Fritzing sketch Schaltplan (saved by Fritzing 0.9.9b)
breadboards: 1

parts:
  R = female pin header, 6 pins [form="♀ (female)"]
  part = Resistor [tolerance=±5% power=0.25 resistance=10k package=THT]
  Arduino_UNO = Arduino Uno (Rev3)
  A+WV = female pin header, 6 pins [form="♀ (female)"]

nets:
  N1: R.pin3, Arduino_UNO.D3_PWM
  N2: R.pin4, Arduino_UNO.GND, A+WV.pin2, A+WV.pin4
  N3: part.Pin_0, Arduino_UNO.A0, A+WV.pin5
  N4: part.Pin_1, Arduino_UNO.5V
  N5: Arduino_UNO.D2, A+WV.pin3

notes:
  Regenmesser
  Anemometer + Windfahne
